// Logisim project Final3exerc.circ as structural Verilog: 1 circuit, main circuit main
module main (
  input  in_1
);

  wire _1_2_out, _1_out, _2_2_out, _2_3_out, _2_4_out, _2_out, _5_2_out, _5_out, clock_1_out, d_ff_1_q,
       d_ff_1_qn, d_ff_2_q, d_ff_2_qn;

  Clock clock_1 (.out(clock_1_out));
  D_Flip_Flop d_ff_1 (.clk(clock_1_out), .D(_2_3_out), .Q(d_ff_1_q), .Qn(d_ff_1_qn));  // open: preset, en, reset
  D_Flip_Flop d_ff_2 (.clk(clock_1_out), .D(_5_2_out), .Q(d_ff_2_q), .Qn(d_ff_2_qn));  // open: preset, en, reset
  nand _2 (_2_out, in_1, in_1);
  nand _2_2 (_2_2_out, _2_out, d_ff_1_q);
  nand _1 (_1_out, in_1, d_ff_2_qn, d_ff_1_qn);
  nand _5 (_5_out, d_ff_1_q, d_ff_2_q);
  nand _2_3 (_2_3_out, _2_2_out, _1_out);
  nand _1_2 (_1_2_out, d_ff_1_q, _2_out, d_ff_2_q);
  nand _5_2 (_5_2_out, _2_2_out, _5_out);
  LED led_1 (.in(_2_4_out));
  nand _2_4 (_2_4_out, _1_out, _1_2_out);

  // Notes on the sheet:
  //   12
  //   13
  //   11
  //   9
  //   10
  //   11
  //   10
  //   9
  //   12
  //   13
  //   8
  //   8
  //   11
  //   1
  //   2
  //   3
  //   4
  //   5
  //   9
  //   10
  //   3
  //   4
  //   6
  //   5
  //   8
  //   6
endmodule
