// Logisim project uklad.circ as structural Verilog: 1 circuit, main circuit main
module main (
  input  in_1,
  input  in_2,
  input  in_3,
  input  in_4
);

  wire clock_1_out, clock_2_out, clock_3_out, d_ff_1_q, d_ff_1_qn, d_ff_2_q, d_ff_2_qn, d_ff_3_q, d_ff_3_qn,
       d_ff_4_q, d_ff_4_qn, j_k_ff_1_q, nand_1_out, nand_2_out, nand_3_out, nand_4_out, nand_5_out,
       nand_6_out, nand_7_out, nand_8_out, nand_9_out, nand_10_out, nand_11_out, nand_12_out, nand_13_out,
       nand_14_out, not_1_out, not_2_out, xor_1_out;

  Clock clock_1 (.out(clock_1_out));
  D_Flip_Flop d_ff_1 (.clk(clock_1_out), .D(nand_8_out), .Q(d_ff_1_q), .Qn(d_ff_1_qn));  // open: preset, en, reset
  D_Flip_Flop d_ff_2 (.clk(clock_1_out), .D(nand_5_out), .Q(d_ff_2_q), .Qn(d_ff_2_qn));  // open: preset, en, reset
  nand nand_1 (nand_1_out, in_1, d_ff_1_qn, d_ff_2_qn);
  nand nand_2 (nand_2_out, d_ff_2_qn, d_ff_1_qn);
  nand nand_3 (nand_3_out, d_ff_2_qn, d_ff_1_q);
  not not_1 (not_1_out, in_1);
  nand nand_4 (nand_4_out, in_1, d_ff_1_q, d_ff_2_q);
  nand nand_5 (nand_5_out, nand_3_out, nand_2_out);
  nand nand_6 (nand_6_out, not_1_out, d_ff_2_qn, d_ff_1_q);
  nand nand_7 (nand_7_out, not_1_out, d_ff_1_qn, d_ff_2_q);
  nand nand_8 (nand_8_out, nand_1_out, nand_7_out, nand_4_out, nand_6_out);
  Clock clock_2 (.out(clock_2_out));
  Clock clock_3 (.out(clock_3_out));
  D_Flip_Flop d_ff_3 (.clk(clock_2_out), .D(nand_14_out), .Q(d_ff_3_q), .Qn(d_ff_3_qn));  // open: preset, en, reset
  D_Flip_Flop d_ff_4 (.clk(clock_2_out), .D(nand_13_out), .Q(d_ff_4_q), .Qn(d_ff_4_qn));  // open: preset, en, reset
  J_K_Flip_Flop j_k_ff_1 (.J(in_3), .clk(clock_3_out), .K(in_3), .Q(j_k_ff_1_q));  // open: Qn, preset, en, reset
  J_K_Flip_Flop j_k_ff_2 (.J(xor_1_out), .clk(clock_3_out), .K(xor_1_out));  // open: Q, Qn, preset, en, reset
  not not_2 (not_2_out, in_4);
  nand nand_9 (nand_9_out, in_4, d_ff_4_qn);
  nand nand_10 (nand_10_out, not_2_out, d_ff_3_qn);
  nand nand_11 (nand_11_out, in_4, d_ff_3_q);
  nand nand_12 (nand_12_out, not_2_out, d_ff_4_q);
  xor xor_1 (xor_1_out, in_2, j_k_ff_1_q);
  nand nand_13 (nand_13_out, nand_10_out, nand_11_out);
  nand nand_14 (nand_14_out, nand_12_out, nand_9_out);
endmodule
